// Logisim project ODS_3.circ as structural Verilog: 1 circuit, main circuit main
module main (
  input  [7:0] in_1,
  input  [7:0] in_2,
  output [7:0] out_3,
  output out_4,
  output [7:0] out_5
);

  wire and_1_out, and_2_out, and_3_out, and_4_out, and_5_out, and_6_out, and_7_out, and_8_out, and_9_out,
       and_10_out, and_11_out, and_12_out, and_13_out, and_14_out, and_15_out, and_16_out, and_17_out,
       and_18_out, and_19_out, and_20_out, and_21_out, and_22_out, and_23_out, and_24_out, and_25_out,
       and_26_out, and_27_out, and_28_out, and_29_out, and_30_out, and_31_out, and_32_out, and_33_out,
       and_34_out, and_35_out, and_36_out, and_37_out, and_38_out, and_39_out, and_40_out, and_41_out,
       and_42_out, and_43_out, and_44_out, and_45_out, and_46_out, and_47_out, and_48_out, and_49_out,
       and_50_out, and_51_out, and_52_out, and_53_out, and_54_out, and_55_out, and_56_out, not_1_out,
       not_2_out, not_3_out, not_4_out, not_5_out, not_6_out, not_7_out, not_8_out, not_9_out, not_10_out,
       not_11_out, not_12_out, not_13_out, not_14_out, not_15_out, not_16_out, not_17_out, not_18_out,
       not_19_out, not_20_out, not_21_out, not_22_out, not_23_out, not_24_out, not_25_out, not_26_out,
       not_27_out, not_28_out, not_29_out, not_30_out, not_31_out, not_32_out, not_33_out, not_34_out,
       not_35_out, not_36_out, not_37_out, not_38_out, not_39_out, not_40_out, not_41_out, not_42_out,
       not_43_out, not_44_out, not_45_out, not_46_out, not_47_out, not_48_out;

  // Probe on in_1
  // Probe on in_2
  // Probe on {out_3[7:1], 1'b0}
  // Probe on out_5
  and and_1 (and_1_out, in_1[0], in_2[0]);
  and and_2 (and_2_out, in_1[0], 1'b0);
  and and_3 (and_3_out, in_2[0], 1'b0);
  not not_1 (not_1_out, in_1[0]);
  not not_2 (not_2_out, 1'b0);
  not not_3 (not_3_out, in_2[0]);
  not not_4 (not_4_out, 1'b0);
  not not_5 (not_5_out, in_1[0]);
  not not_6 (not_6_out, in_2[0]);
  and and_4 (and_4_out, in_1[0], in_2[0], 1'b0);
  and and_5 (and_5_out, not_1_out, in_2[0], not_2_out);
  and and_6 (and_6_out, in_1[0], not_3_out, not_4_out);
  and and_7 (and_7_out, not_5_out, not_6_out, 1'b0);
  or P_2 (out_3[1], and_1_out, and_2_out, and_3_out);
  or S_2 (out_5[0], and_4_out, and_5_out, and_6_out, and_7_out);
  and and_8 (and_8_out, in_1[1], in_2[1]);
  and and_9 (and_9_out, in_1[1], out_3[1]);
  and and_10 (and_10_out, in_2[1], out_3[1]);
  and and_11 (and_11_out, in_1[1], in_2[1], out_3[1]);
  not not_7 (not_7_out, in_1[1]);
  and and_12 (and_12_out, not_7_out, in_2[1], not_8_out);
  not not_8 (not_8_out, out_3[1]);
  and and_13 (and_13_out, in_1[1], not_9_out, not_10_out);
  not not_9 (not_9_out, in_2[1]);
  not not_10 (not_10_out, out_3[1]);
  not not_11 (not_11_out, in_1[1]);
  not not_12 (not_12_out, in_2[1]);
  and and_14 (and_14_out, not_11_out, not_12_out, out_3[1]);
  or P_3 (out_3[2], and_8_out, and_9_out, and_10_out);
  or S_3 (out_5[1], and_11_out, and_12_out, and_13_out, and_14_out);
  not not_13 (not_13_out, in_1[2]);
  not not_14 (not_14_out, out_3[2]);
  not not_15 (not_15_out, in_2[2]);
  not not_16 (not_16_out, out_3[2]);
  not not_17 (not_17_out, in_1[2]);
  not not_18 (not_18_out, in_2[2]);
  and and_15 (and_15_out, in_1[2], in_2[2]);
  and and_16 (and_16_out, in_1[2], out_3[2]);
  and and_17 (and_17_out, in_2[2], out_3[2]);
  and and_18 (and_18_out, in_1[2], in_2[2], out_3[2]);
  and and_19 (and_19_out, not_13_out, in_2[2], not_14_out);
  and and_20 (and_20_out, in_1[2], not_15_out, not_16_out);
  and and_21 (and_21_out, not_17_out, not_18_out, out_3[2]);
  or P_4 (out_3[3], and_15_out, and_16_out, and_17_out);
  or S_4 (out_5[2], and_18_out, and_19_out, and_20_out, and_21_out);
  not not_19 (not_19_out, in_1[3]);
  not not_20 (not_20_out, out_3[3]);
  not not_21 (not_21_out, in_2[3]);
  not not_22 (not_22_out, out_3[3]);
  not not_23 (not_23_out, in_1[3]);
  not not_24 (not_24_out, in_2[3]);
  and and_22 (and_22_out, in_1[3], in_2[3]);
  and and_23 (and_23_out, in_1[3], out_3[3]);
  and and_24 (and_24_out, in_2[3], out_3[3]);
  and and_25 (and_25_out, in_1[3], in_2[3], out_3[3]);
  and and_26 (and_26_out, not_19_out, in_2[3], not_20_out);
  and and_27 (and_27_out, in_1[3], not_21_out, not_22_out);
  and and_28 (and_28_out, not_23_out, not_24_out, out_3[3]);
  or P_5 (out_3[4], and_22_out, and_23_out, and_24_out);
  or S_5 (out_5[3], and_25_out, and_26_out, and_27_out, and_28_out);
  and and_29 (and_29_out, in_1[4], in_2[4]);
  and and_30 (and_30_out, in_1[4], out_3[4]);
  and and_31 (and_31_out, in_2[4], out_3[4]);
  not not_25 (not_25_out, in_1[4]);
  not not_26 (not_26_out, out_3[4]);
  not not_27 (not_27_out, in_2[4]);
  not not_28 (not_28_out, out_3[4]);
  not not_29 (not_29_out, in_1[4]);
  not not_30 (not_30_out, in_2[4]);
  and and_32 (and_32_out, in_1[4], in_2[4], out_3[4]);
  and and_33 (and_33_out, not_25_out, in_2[4], not_26_out);
  and and_34 (and_34_out, in_1[4], not_27_out, not_28_out);
  and and_35 (and_35_out, not_29_out, not_30_out, out_3[4]);
  or P_6 (out_3[5], and_29_out, and_30_out, and_31_out);
  or S_6 (out_5[4], and_32_out, and_33_out, and_34_out, and_35_out);
  and and_36 (and_36_out, in_1[5], in_2[5]);
  and and_37 (and_37_out, in_1[5], out_3[5]);
  and and_38 (and_38_out, in_2[5], out_3[5]);
  and and_39 (and_39_out, in_1[5], in_2[5], out_3[5]);
  not not_31 (not_31_out, in_1[5]);
  and and_40 (and_40_out, not_31_out, in_2[5], not_32_out);
  not not_32 (not_32_out, out_3[5]);
  not not_33 (not_33_out, in_2[5]);
  and and_41 (and_41_out, in_1[5], not_33_out, not_34_out);
  not not_34 (not_34_out, out_3[5]);
  not not_35 (not_35_out, in_1[5]);
  not not_36 (not_36_out, in_2[5]);
  and and_42 (and_42_out, not_35_out, not_36_out, out_3[5]);
  or P_7 (out_3[6], and_36_out, and_37_out, and_38_out);
  or S_7 (out_5[5], and_39_out, and_40_out, and_41_out, and_42_out);
  not not_37 (not_37_out, in_1[6]);
  not not_38 (not_38_out, out_3[6]);
  not not_39 (not_39_out, in_2[6]);
  not not_40 (not_40_out, out_3[6]);
  not not_41 (not_41_out, in_1[6]);
  not not_42 (not_42_out, in_2[6]);
  and and_43 (and_43_out, in_1[6], in_2[6]);
  and and_44 (and_44_out, in_1[6], out_3[6]);
  and and_45 (and_45_out, in_2[6], out_3[6]);
  and and_46 (and_46_out, in_1[6], in_2[6], out_3[6]);
  and and_47 (and_47_out, not_37_out, in_2[6], not_38_out);
  and and_48 (and_48_out, in_1[6], not_39_out, not_40_out);
  and and_49 (and_49_out, not_41_out, not_42_out, out_3[6]);
  or P_8 (out_3[7], and_43_out, and_44_out, and_45_out);
  or S_8 (out_5[6], and_46_out, and_47_out, and_48_out, and_49_out);
  not not_43 (not_43_out, in_1[7]);
  not not_44 (not_44_out, out_3[7]);
  not not_45 (not_45_out, in_2[7]);
  not not_46 (not_46_out, out_3[7]);
  not not_47 (not_47_out, in_1[7]);
  not not_48 (not_48_out, in_2[7]);
  and and_50 (and_50_out, in_1[7], in_2[7]);
  and and_51 (and_51_out, in_1[7], out_3[7]);
  and and_52 (and_52_out, in_2[7], out_3[7]);
  and and_53 (and_53_out, in_1[7], in_2[7], out_3[7]);
  and and_54 (and_54_out, not_43_out, in_2[7], not_44_out);
  and and_55 (and_55_out, in_1[7], not_45_out, not_46_out);
  and and_56 (and_56_out, not_47_out, not_48_out, out_3[7]);
  or P_9 (out_4, and_50_out, and_51_out, and_52_out);
  or S_9 (out_5[7], and_53_out, and_54_out, and_55_out, and_56_out);

  assign out_3[0] = 1'b0;
endmodule
