// Logisim project lab5.circ as structural Verilog: 1 circuit, main circuit main
module main (
);

  wire and_1_out, and_2_out, clock_1_out;
  wire [2:0] T1_q;

  and and_1 (and_1_out, 1'b1, T1_q[0], T1_q[1]);
  and and_2 (and_2_out, 1'b1, T1_q[0]);
  Clock #(.lowDuration(14)) clock_1 (.out(clock_1_out));
  T_Flip_Flop T3 (.clk(clock_1_out), .T(and_1_out), .Q(T1_q[2]));  // open: Qn, preset, reset, en
  T_Flip_Flop T2 (.clk(clock_1_out), .T(and_2_out), .Q(T1_q[1]));  // open: Qn, preset, reset, en
  T_Flip_Flop T1 (.clk(clock_1_out), .T(1'b1), .Q(T1_q[0]));  // open: Qn, preset, reset, en
  // Probe on T1_q
endmodule
